// Digital circuit Final_draf.dig as structural Verilog
module Final_draf (
  input  [8:0] N,
  input  reset,
  input  start,
  input  clock,
  output [7:0] displayout,
  output done,
  output [15:0] clockcount,
  output valid
);

  wire add_data, and_1_out, and_2_out, and_3_out, and_9_out, clk1, clk3, clk7, clk_count, comparator_1_eq,
       comparator_1_gt, comparator_1_lt, comparator_2_eq, comparator_2_gt, comparator_4_eq, comparator_5_eq,
       comparator_5_gt, comparator_5_lt, count_print, count_yes, d_ff_1_q, end_sta1, end_sta3,
       multiplexer_1_out, multiplexer_2_out, multiplexer_3_out, N_eq_0, next_num, not_1_out, not_2_out,
       not_3_out, not_4_out, not_5_out, not_6_out, not_7_out, or_1_out, or_2_out, or_5_out, or_6_out,
       or_8_out, or_9_out, or_10_out, or_11_out, or_12_out, or_14_out, or_15_out, or_16_out, or_17_out,
       or_18_out, or_21_out, re4, s0_plus_s4, sta0, sta1, sta2, sta3, sta4, sta5, sta7;
  wire [1:1] or_13_out;
  wire [2:0] register_3_q;
  wire [7:0] multiplexer_10_out, ROMFILE_d;
  wire [8:0] add_2_s, add_3_s, add_4_s, add_5_s, Count1_q, Count3_q, multiplexer_5_out, multiplexer_7_out,
       multiplexer_8_out, multiplexer_9_out, multiplexer_11_out, now_slot_q, num;
  wire [9:0] add_6_s, multiplexer_12_out, multiplexer_13_out, Proc_RAM_d, sub_1_s;
  wire [15:0] add_1_s, clk_count_q, multiplexer_4_out;

  or or_1 (or_1_out, end_sta1, N_eq_0);
  not not_1 (not_1_out, start);
  not not_2 (not_2_out, N_eq_0);
  not not_3 (not_3_out, end_sta3);
  Multiplexer #(.Selector_Bits(3)) multiplexer_1 (
    .sel(register_3_q), .in_0(1'b1), .in_1(or_1_out), .in_2(1'b1), .in_3(1'b0), .in_4(not_1_out),
    .in_5(1'b0), .in_6(1'b1), .in_7(1'b1), .out(multiplexer_1_out));
  Multiplexer #(.Selector_Bits(3)) multiplexer_2 (
    .sel(register_3_q), .in_0(1'b0), .in_1(N_eq_0), .in_2(1'b1), .in_3(1'b1), .in_4(1'b0), .in_5(1'b1),
    .in_6(1'b1), .in_7(1'b1), .out(multiplexer_2_out));
  Multiplexer #(.Selector_Bits(3)) multiplexer_3 (
    .sel(register_3_q), .in_0(1'b0), .in_1(not_2_out), .in_2(1'b1), .in_3(not_3_out), .in_4(start),
    .in_5(1'b1), .in_6(1'b0), .in_7(count_print), .out(multiplexer_3_out));
  and and_1 (and_1_out, multiplexer_1_out, not_4_out);
  not not_4 (not_4_out, reset);
  and and_2 (and_2_out, multiplexer_2_out, not_5_out);
  not not_5 (not_5_out, reset);
  and and_3 (and_3_out, multiplexer_3_out, not_6_out);
  not not_6 (not_6_out, reset);
  Register register_1 (.D(and_1_out), .C(clock), .en(1'b1), .Q(register_3_q[2]));
  Register register_2 (.D(and_2_out), .C(clock), .en(1'b1), .Q(register_3_q[1]));
  Register register_3 (.D(and_3_out), .C(clock), .en(1'b1), .Q(register_3_q[0]));
  Decoder #(.Selector_Bits(3)) decoder_1 (
    .sel(register_3_q), .out_0(sta0), .out_1(sta1), .out_2(sta2), .out_3(sta3), .out_4(sta4), .out_5(sta5),
    .out_6(done), .out_7(sta7));
  Comparator #(.Bits(9)) comparator_1 (
    .a(num), .b(9'h100), .gt(comparator_1_gt), .eq(comparator_1_eq), .lt(comparator_1_lt));
  or or_2 (or_2_out, sta1, sta2, sta3, sta5, sta7);
  not not_7 (not_7_out, sta4);
  D_FF d_ff_1 (.D(not_7_out), .C(clock), .Q(d_ff_1_q));  // open: nQ
  or or_3 (s0_plus_s4, sta0, sta4);
  and and_4 (clk_count, or_2_out, clock);
  and and_5 (clk1, sta1, clock);
  and and_6 (clk7, sta7, clock);
  or or_4 (end_sta3, comparator_1_gt, comparator_1_eq);
  and and_7 (clk3, comparator_1_lt, sta3, clock);
  Comparator #(.Bits(9)) u_N_eq_0 (.a(N), .b({9{1'b0}}), .eq(N_eq_0));  // open: gt, lt
  and and_8 (re4, sta4, d_ff_1_q);
  Add #(.Bits(16)) add_1 (.a(clk_count_q), .b(16'h1), .c_i(1'b0), .s(add_1_s));  // open: c_o
  Add #(.Bits(9)) add_2 (.a(Count1_q), .b(9'h1), .c_i(1'b0), .s(add_2_s));  // open: c_o
  Multiplexer #(.Bits(16)) multiplexer_4 (.sel(s0_plus_s4), .in_0(add_1_s), .in_1({16{1'b0}}), .out(multiplexer_4_out));
  Multiplexer #(.Bits(9)) multiplexer_5 (.sel(s0_plus_s4), .in_0(add_2_s), .in_1({9{1'b0}}), .out(multiplexer_5_out));
  or or_5 (or_5_out, re4, clk_count);
  or or_6 (or_6_out, re4, clk1);
  Register #(.Bits(16)) u_clk_count (.D(multiplexer_4_out), .C(or_5_out), .en(1'b1), .Q(clk_count_q));
  Register #(.Bits(9)) Count1 (.D(multiplexer_5_out), .C(or_6_out), .en(1'b1), .Q(Count1_q));
  Comparator #(.Bits(9)) comparator_2 (.a(Count1_q), .b(N), .gt(comparator_2_gt), .eq(comparator_2_eq), .lt(count_yes));
  Multiplexer #(.Bits(16)) multiplexer_6 (.sel(done), .in_0({16{1'b0}}), .in_1(clk_count_q), .out(clockcount));
  ROM #(.AddrBits(9), .Bits(8)) ROMFILE (.A(Count1_q), .sel(1'b1), .D(ROMFILE_d));
  or or_7 (end_sta1, comparator_2_gt, comparator_2_eq);
  Add #(.Bits(9)) add_3 (.a(num), .b(9'h1), .c_i(1'b0), .s(add_3_s));  // open: c_o
  Add #(.Bits(9)) add_4 (.a(now_slot_q), .b(9'h1), .c_i(1'b0), .s(add_4_s));  // open: c_o
  Add #(.Bits(9)) add_5 (.a(Count3_q), .b(9'h1), .c_i(1'b0), .s(add_5_s));  // open: c_o
  Multiplexer #(.Bits(9)) multiplexer_7 (.sel(s0_plus_s4), .in_0(add_3_s), .in_1({9{1'b0}}), .out(multiplexer_7_out));
  Multiplexer #(.Bits(9)) multiplexer_8 (.sel(s0_plus_s4), .in_0(add_4_s), .in_1({9{1'b0}}), .out(multiplexer_8_out));
  Multiplexer #(.Bits(9)) multiplexer_9 (.sel(s0_plus_s4), .in_0(add_5_s), .in_1({9{1'b0}}), .out(multiplexer_9_out));
  or or_8 (or_8_out, re4, clk3);
  or or_9 (or_9_out, re4, clk3);
  or or_10 (or_10_out, re4, clk7);
  Multiplexer #(.Selector_Bits(2), .Bits(8)) multiplexer_10 (
    .sel({or_13_out[1], sta1}), .in_0({8{1'b0}}), .in_1(ROMFILE_d), .in_2(num[7:0]), .in_3({8{1'b0}}),
    .out(multiplexer_10_out));
  or or_11 (or_11_out, next_num, s0_plus_s4);
  Register #(.Bits(9)) now_slot (.D(multiplexer_8_out), .C(or_9_out), .en(or_12_out), .Q(now_slot_q));
  or or_12 (or_12_out, add_data, s0_plus_s4);
  or or_13 (or_13_out[1], sta3, sta5);
  Register #(.Bits(9)) Count2 (.D(multiplexer_7_out), .C(or_8_out), .en(or_11_out), .Q(num));
  Register #(.Bits(9)) Count3 (.D(multiplexer_9_out), .C(or_10_out), .en(1'b1), .Q(Count3_q));
  or or_14 (or_14_out, count_yes, sta3);
  RAMDualPort #(.AddrBits(8), .Bits(10)) Proc_RAM (
    .A(multiplexer_10_out), .Din(multiplexer_13_out), .str(or_14_out), .C(or_15_out), .ld(1'b1),
    .D(Proc_RAM_d));
  or or_15 (or_15_out, clk1, clk3);
  Comparator #(.Bits(9)) comparator_3 (.a(Count3_q), .b(N), .lt(count_print));  // open: gt, eq
  or or_16 (or_16_out, sta7, sta2);
  Multiplexer #(.Bits(9)) multiplexer_11 (
    .sel(or_16_out), .in_0(now_slot_q), .in_1(Count3_q), .out(multiplexer_11_out));
  or or_17 (or_17_out, clk3, clk7);
  and and_9 (and_9_out, count_print, or_18_out);
  Add #(.Bits(10)) add_6 (.a(Proc_RAM_d), .b(10'h1), .c_i(1'b0), .s(add_6_s));  // open: c_o
  Sub #(.Bits(10)) sub_1 (.a(Proc_RAM_d), .b(10'h1), .c_i(1'b0), .s(sub_1_s));  // open: c_o
  Comparator #(.Bits(10)) comparator_4 (.a(Proc_RAM_d), .b({10{1'b0}}), .eq(comparator_4_eq));  // open: gt, lt
  Comparator #(.Bits(10)) comparator_5 (
    .a(Proc_RAM_d), .b(10'h1), .gt(comparator_5_gt), .eq(comparator_5_eq), .lt(comparator_5_lt));
  RAMDualPort #(.AddrBits(9), .Bits(8)) RAM (
    .A(multiplexer_11_out), .Din(num[7:0]), .str(add_data), .C(or_17_out), .ld(and_9_out), .D(displayout));
  or or_18 (or_18_out, sta2, sta7);
  Multiplexer #(.Bits(10)) multiplexer_12 (
    .sel(comparator_4_eq), .in_0(sub_1_s), .in_1({10{1'b0}}), .out(multiplexer_12_out));
  or or_19 (add_data, comparator_5_gt, comparator_5_eq);
  or or_20 (next_num, comparator_5_eq, comparator_5_lt);
  Multiplexer #(.Selector_Bits(2), .Bits(10)) multiplexer_13 (
    .sel({sta3, sta1}), .in_0({10{1'b0}}), .in_1(add_6_s), .in_2(multiplexer_12_out), .in_3({10{1'b0}}),
    .out(multiplexer_13_out));
  Seven_Seg_Hex seven_seg_hex_1 (.d(displayout[7:4]), .dp(1'b0));
  or or_21 (or_21_out, sta2, sta7);
  Seven_Seg_Hex seven_seg_hex_2 (.d(displayout[3:0]), .dp(1'b0));
  and and_10 (valid, count_print, or_21_out);

  // Other names for the same wires on the sheet: ans_clock[15:0] = clockcount; clk = clock; res = reset; sta6 = done;
  //   start_button = start

  // Notes on the sheet:
  //   clock: Hz: 20
  //   contents of ROMFILE (hex, n*v repeats v):
  //   f0,f7,f5,f8,f2
endmodule
